# Fritzing sketch ESTAÇAO DE COMANDO (saved by Fritzing 1.0.1rc)

parts:
  LED2 = Yellow LED - Rect 5x2x7mm [package="5x2x7 mm [THT]"]  # not connected
  R3 = Resistor [tolerance=±5% resistance=220 package="1206 [SMD]"]
  S2 = Illuminated Pushbutton
  LED1 = Red LED - Rect 5x2x7mm [package="5x2x7 mm [THT]"]
  S1 = Toggle Switch spst [package=THT]
  Mod1 = Raspberry Pi Pico
  buz1 = Piezo Buzzer
  R4 = Resistor [tolerance=±5% resistance=220 package="1206 [SMD]"]
  M1 = Osoyoo SX1278-ra-02
  TP1 = TP4056 [chip_label=TP4056 package="DIP (Dual Inline) [THT]"]
  VCC1 = Battery
  R5 = Resistor [tolerance=±5% resistance=220 package="1206 [SMD]"]

nets:
  N1: R3.Pin_0, Mod1.pin_16
  N2: S2.S-1, LED1.anode, Mod1.pin_3, Mod1.pin_28, Mod1.pin_33, Mod1.pin_38, Mod1.pin_42, buz1.pin_2, M1.GND, TP1.pin6
  N3: S2.LED-, R5.Pin_1
  N4: S2.S-2, Mod1.pin_17
  N5: LED1.cathode, R4.Pin_1
  N6: S1.COM, TP1.pin4
  N7: Mod1.pin_1, M1.MOSI
  N8: Mod1.pin_2, M1.NSS
  N9: Mod1.pin_4, M1.SCK
  N10: Mod1.pin_5, M1.MISO
  N11: Mod1.pin_6, M1.RST
  N12: Mod1.pin_15, R4.Pin_0
  N13: Mod1.pin_25, buz1.pin_1
  N14: Mod1.pin_31, R5.Pin_0
  N15: Mod1.pin_36, M1.3.3V
  N16: Mod1.pin_39, TP1.pin3
  N17: TP1.pin5, VCC1.-

custom parts:
  Yellow LED - Rect 5x2x7mm: A generic rectangular yellow LED (~1.8V) 5mm x 2mm x 7mm
  Red LED - Rect 5x2x7mm: A generic rectangular red LED (~1.8V) 5mm x 2mm x 7mm
  Toggle Switch spst: Toggle Switch single pole single throw
  Raspberry Pi Pico: Raspberry Pi Pico. Based around the RP2040 microcontroller the Pico is a low cost microcontroller device bringing Raspberry Pi quality, cost, and easy of use to the microcontroller space. Jan 2021, Split part in to two versions: tht (this one) and SMD. This one will drill holes for a .1 in header in pcb to allow plugging in the module as well as providing pads to solder the module to the top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
  Piezo Buzzer: Part from https://www.nutsvolts.com/magazine/article/november2012_SmileysWorkshop modified to be .3 in spacing to match the adafruit buzzer 5V breadboard friendly part.
  Osoyoo SX1278-ra-02: Osoyoo Long Distance wireless transceiver Uart LoRa Module.
  TP4056: A DIP stand-in part for whatever IC you want. With 6 pins on a 300mil dual inline package (DIP) footprint.
  Battery: Your standard 2x 18650 battery pack (7.4 Volts)
