# Fritzing sketch ESTAÇÃO DE IGNIÇÃO (saved by Fritzing 1.0.1rc)

parts:
  LED2 = Yellow LED - Rect 5x2x7mm [package="5x2x7 mm [THT]"]
  R3 = Resistor [tolerance=±5% resistance=220 package="1206 [SMD]"]
  LED1 = Red LED - Rect 5x2x7mm [package="5x2x7 mm [THT]"]
  S1 = Toggle Switch spst [package=THT]
  Mod1 = Raspberry Pi Pico
  buz1 = Piezo Buzzer
  R4 = Resistor [tolerance=±5% resistance=220 package="1206 [SMD]"]
  M1 = Osoyoo SX1278-ra-02
  M2 = 1 chan 5v relay module
  LED4 = Blue LED - Rect 5x2x7mm [package="5x2x7 mm [THT]"]
  TP2 = TP4056 [chip_label=TP4056 package="DIP (Dual Inline) [THT]"]
  BAT1 = 18650 battery holder [package=battery-18650-kit]
  BAT2 = 18650 battery holder [package=battery-18650-kit]
  VCC1 = Battery

nets:
  N1: LED2.anode, LED1.anode, Mod1.pin_3, Mod1.pin_23, Mod1.pin_28, Mod1.pin_33, Mod1.pin_38, Mod1.pin_42, buz1.pin_2, M1.GND, M2.pin_2, TP2.pin5
  N2: R3.Pin_0, Mod1.pin_16
  N3: S1.COM, TP2.pin4
  N4: Mod1.pin_1, M1.MOSI
  N5: Mod1.pin_2, M1.NSS
  N6: Mod1.pin_4, M1.SCK
  N7: Mod1.pin_5, M1.MISO
  N8: Mod1.pin_6, M1.RST
  N9: Mod1.pin_15, R4.Pin_0
  N10: Mod1.pin_25, buz1.pin_1
  N11: Mod1.pin_31, M2.pin_3
  N12: Mod1.pin_36, M1.3.3V
  N13: Mod1.pin_39, TP2.pin3
  N14: Mod1.pin_40, M2.pin_1
  N15: M2.pin_4, LED4.cathode
  N16: M2.pin_5, VCC1.+
  N17: M2.pin_6, LED4.anode, VCC1.-
  N18: BAT1.+, BAT2.+
  N19: BAT1.-, BAT2.-

custom parts:
  Yellow LED - Rect 5x2x7mm: A generic rectangular yellow LED (~1.8V) 5mm x 2mm x 7mm
  Red LED - Rect 5x2x7mm: A generic rectangular red LED (~1.8V) 5mm x 2mm x 7mm
  Toggle Switch spst: Toggle Switch single pole single throw
  Raspberry Pi Pico: Raspberry Pi Pico. Based around the RP2040 microcontroller the Pico is a low cost microcontroller device bringing Raspberry Pi quality, cost, and easy of use to the microcontroller space. Jan 2021, Split part in to two versions: tht (this one) and SMD. This one will drill holes for a .1 in header in pcb to allow plugging in the module as well as providing pads to solder the module to the top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
  Piezo Buzzer: Part from https://www.nutsvolts.com/magazine/article/november2012_SmileysWorkshop modified to be .3 in spacing to match the adafruit buzzer 5V breadboard friendly part.
  Osoyoo SX1278-ra-02: Osoyoo Long Distance wireless transceiver Uart LoRa Module.
  1 chan 5v relay module: 1 Channel 5V Relay Module Board Shield with Optocoupler Support High and Low Level Trigger for Arduino.
  Blue LED - Rect 5x2x7mm: A generic rectangular blue LED (~1.8V) 5mm x 2mm x 7mm
  TP4056: A DIP stand-in part for whatever IC you want. With 6 pins on a 300mil dual inline package (DIP) footprint.
  18650 battery holder: 18650 Battery
  Battery: Your standard 2x 18650 battery pack (14.7 Volts)
